# Fritzing sketch blueprint (saved by Fritzing 0.9.3b)

parts:
  Componente1 = Arduino Uno (Rev3)
  MFS1 = Multi Function Shield

nets:
  N1: Componente1.D8, MFS1.D8
  N2: Componente1.D4, MFS1.D4
  N3: Componente1.D7, MFS1.D7

custom parts:
  Multi Function Shield: Das Multi Function Shield kann auf den Arduino Uno aufgesteckt werden und bietet ein paar wichtige Bauteile.
